# Fritzing sketch Biosynth-001r (saved by Fritzing 0.9.4)
breadboards: 1

parts:
  R1 = Resistor [tolerance=±5% resistance=3.3k package=THT]
  R2 = Resistor [tolerance=±5% resistance=1k package=THT]  # not connected
  R3 = Resistor [tolerance=±5% resistance=1M package=THT]
  R7 = Resistor [tolerance=±5% resistance=10 package=THT]
  R8 = Resistor [tolerance=±5% resistance=3.3M package=THT]
  R9 = Resistor [tolerance=±5% resistance=3.3k package=THT]
  R10 = Resistor [tolerance=±5% resistance=3.3M package=THT]
  R11 = Resistor [tolerance=±5% resistance=10k package=THT]
  R12 = Resistor [tolerance=±5% resistance=100k package=THT]
  C1 = Tantalum Capacitor [capacitance=100nF package="100 mil [THT, tantalum]"]
  C2 = Tantalum Capacitor [capacitance=100nF package="100 mil [THT, tantalum]"]  # not connected
  C4 = Tantalum Capacitor [capacitance=10nF package="100 mil [THT, tantalum]"]
  IC1 = Dual Op-Amp [part_number=MCP6002 package=dip08]
  J1 = screw terminal, 3 pins [part_number="Pulse Signal"]
  J2 = Screw terminal - 2 pins [part_number=ED1623-ND package=THT]
  J3 = Screw terminal - 2 pins [part_number=ED1623-ND package=THT]  # not connected
  C3 = Electrolytic Capacitor [capacitance=220µF package="100 mil [THT, electrolytic]"]  # not connected
  C5 = Electrolytic Capacitor [capacitance=220µF package="100 mil [THT, electrolytic]"]
  R13 = Temperature Sensor (Thermistor) [thermistor_type=NTC part_number=Thermistor package=THT]
  U1 = DCM01 Reflective Blood Sensor [part_number=pulsesensor package=dcm01]  # not connected
  J4 = screw terminal, 3 pins  # not connected
  J5 = screw terminal, 3 pins
  Part1 = Arduino Nano (Rev3.0)

nets (from the schematic view):
  N1: R1.Pin_0, R7.Pin_0, R11.Pin_1, J1.pin1, Part1.GND
  N2: R1.Pin_1, IC1.B_+IN, R13.pin_0
  N3: R3.Pin_0, R12.Pin_1, C4.-, IC1.B_-IN
  N4: R3.Pin_1, C4.+, IC1.B_OUT, J5.pin2
  N5: R7.Pin_1, R8.Pin_0, J2.pin1
  N6: R8.Pin_1, R10.Pin_0, C1.+, IC1.A_-IN
  N7: R9.Pin_0, R11.Pin_0, IC1.A_+IN
  N8: R9.Pin_1, J2.pin2, Part1.5V
  N9: R10.Pin_1, C1.-, IC1.A_OUT
  N10: R12.Pin_0, C5.+
  N11: J1.pin2, Part1.3V3
  N12: J1.pin3, J5.pin3

notes:
  [I don't see R 4, R5, or R6 on the parts list.]
  an attempt to build
  Erin Gee's
  Biosynth
  v 3.0 2018
  GSR signal
