# Fritzing sketch Biosynth-008 (saved by Fritzing 1.0.2b)
breadboards: 1

parts:
  R1 = Resistor [tolerance=±5% resistance=3.3k power=0.25W package=THT]
  R2 = Resistor [tolerance=±5% resistance=1k power=0.25W package=THT]
  R3 = Resistor [tolerance=±5% resistance=1M power=0.25W package=THT]
  R7 = Resistor [tolerance=±5% resistance=10 power=0.25W package=THT]
  R8 = Resistor [tolerance=±5% resistance=3.3M power=0.25W package=THT]
  R9 = Resistor [tolerance=±5% resistance=3.3k power=0.25W package=THT]
  R10 = Resistor [tolerance=±5% resistance=3.3M power=0.25W package=THT]
  R11 = Resistor [tolerance=±5% resistance=10k power=0.25W package=THT]
  R12 = Resistor [tolerance=±5% resistance=100k power=0.25W package=THT]
  C1 = Tantalum Capacitor [capacitance=100nF voltage=35V package="100 mil [THT, tantalum]"]
  C2 = Tantalum Capacitor [capacitance=100nF package="100 mil [THT, tantalum]"]
  C4 = Tantalum Capacitor [capacitance=10nF voltage=35V package="100 mil [THT, tantalum]"]
  IC1 = Dual Op-Amp [part_number=MCP6002 package=dip08]
  J1 = screw terminal, 3 pins [part_number="Pulse Signal"]
  J2 = Screw terminal - 2 pins [part_number=ED1623-ND package=THT]
  J3 = Screw terminal - 2 pins [part_number=ED1623-ND package=THT]
  C3 = Electrolytic Capacitor [capacitance=220µF voltage=35V package="100 mil [THT, electrolytic]"]
  C5 = Electrolytic Capacitor [capacitance=220µF voltage=35V package="100 mil [THT, electrolytic]"]
  R13 = Temperature Sensor (Thermistor) [thermistor_type=NTC part_number=Thermistor package=THT]  # not connected
  U1 = DCM01 Reflective Blood Sensor [part_number=pulsesensor package=dcm01]  # not connected
  J4 = screw terminal, 3 pins
  J5 = screw terminal, 3 pins  # not connected
  Part1 = Arduino Nano (Rev3.0)
  LED1 = LED - 5mm [color="Red (633nm)" current=0.030A package="5 mm [THT]"]

nets:
  N1: R1.Pin_0, IC1.B_+IN, J3.pin2
  N2: R1.Pin_1, R7.Pin_0, R11.Pin_1, IC1.A_V-, J1.pin1, C5.-, J4.pin2, Part1.GND, LED1.cathode
  N3: R2.Pin_0, R9.Pin_1, C2.+, IC1.A_V+, J2.pin2, C3.+, J4.pin3, Part1.5V
  N4: R2.Pin_1, LED1.anode
  N5: R3.Pin_0, R12.Pin_1, C4.-, IC1.B_-IN
  N6: R3.Pin_1, C4.+, IC1.B_OUT, Part1.A0
  N7: R7.Pin_1, R8.Pin_0, J2.pin1
  N8: R8.Pin_1, R10.Pin_0, C1.+, IC1.A_-IN
  N9: R9.Pin_0, R11.Pin_0, IC1.A_+IN
  N10: R10.Pin_1, C1.-, IC1.A_OUT, Part1.A6
  N11: R12.Pin_0, C5.+
  N12: J1.pin2, J4.pin1, Part1.3V3
  N13: J1.pin3, Part1.A1

notes:
  [I don't see R4, R5, or R6 on the parts list.]
  an attempt to build
  Erin Gee's
  Biosynth
  v 3.0 2018
  Her schematic says J3 should only have one terminal, but I couldn't find a terminal with only one pin.
  Her schematic is using a Teensy, I am using an Arduino Nano here.
  J5 pins are the arduino inputs:
  J5-1 = GSR = A6
  J5-2 = Thermistor = A0
  J5-3 = Pulse = A1
