# Fritzing sketch Biosynthv3-240323_BB (saved by Fritzing 0.9.6b)
breadboards: 1

parts:
  C1 = Ceramic Capacitor [capacitance=0.1µF voltage=35V package="100 mil [THT, multilayer]"]
  R12 = Resistor [tolerance=±5% resistance=100k package="0603 [SMD]"]
  R2 = Resistor [tolerance=±5% resistance=1k package="0603 [SMD]"]
  J5 = screw terminal, 3 pins
  R10 = Resistor [tolerance=±5% resistance=3.3M package="0603 [SMD]"]
  J2 = Screw terminal - 2 pins [package=THT]
  R8 = Resistor [tolerance=±5% resistance=3.3M package="0603 [SMD]"]
  R11 = Resistor [tolerance=±5% resistance=10k package="0603 [SMD]"]
  U2 = Dual Op-Amp [part_number=MCP6002 package=dip08]
  R3 = Resistor [tolerance=±5% resistance=1M package="0603 [SMD]"]
  J3 = Screw terminal - 2 pins [package=THT]
  C3 = Electrolytic Capacitor [capacitance=47µF voltage=35V package="200 mil [THT, electrolytic]"]
  C2 = Ceramic Capacitor [capacitance=0.1µF voltage=35V package="100 mil [THT, multilayer]"]
  R1 = Resistor [tolerance=±5% resistance=3.3k package="0603 [SMD]"]
  C5 = Electrolytic Capacitor [capacitance=220µF voltage=35V package="200 mil [THT, electrolytic]"]
  R9 = Resistor [tolerance=±5% resistance=3.3k package="0603 [SMD]"]
  LED1 = LED - 5mm [color="Red (633nm)" current=0.030 package="5 mm [THT]"]
  J4 = screw terminal, 3 pins
  R7 = Resistor [tolerance=±5% resistance=10M package="0603 [SMD]"]
  J1 = screw terminal, 3 pins
  C4 = Ceramic Capacitor [capacitance=0.01µF voltage=35V package="100 mil [THT, multilayer]"]
  YwRobot_Power_Supply1 = YwRobot Breadboard Power Supply [part_number=545043]

nets:
  N1: C1.0, R10.Pin_0, R8.Pin_1, U2.A_-IN
  N2: C1.1, J5.pin1, R10.Pin_1, U2.A_OUT
  N3: R12.Pin_0, J5.pin2, U2.B_OUT, R3.Pin_1, C4.1
  5V: R12.Pin_1, R2.Pin_1, J2.pin1, U2.A_V+, C3.+, C2.1, C5.+, R9.Pin_1, J4.pin1, YwRobot_Power_Supply1.GND#13, YwRobot_Power_Supply1.GND#14
  N4: R2.Pin_0, LED1.anode
  N5: J5.pin3, J1.pin1
  N6: J2.pin2, R8.Pin_0, R7.Pin_1
  GND: R11.Pin_0, U2.A_V-, C3.-, C2.0, R1.Pin_0, C5.-, LED1.cathode, J4.pin2, R7.Pin_0, J1.pin3
  N7: R11.Pin_1, U2.A_+IN, R9.Pin_0
  N8: U2.B_+IN, J3.pin2, R1.Pin_1
  N9: U2.B_-IN, R3.Pin_0, C4.0
  3.3V: J4.pin3, J1.pin2
  N10: YwRobot_Power_Supply1.VCC#5, YwRobot_Power_Supply1.VCC#6
  N11: YwRobot_Power_Supply1.VCC#9, YwRobot_Power_Supply1.VCC#10
  N12: YwRobot_Power_Supply1.GND#11, YwRobot_Power_Supply1.GND#12

notes:
  THERMISTOR_SIG
  PULSE_SIG
  GSR_SIG
  Thermistor (10k NTC)
  GSR-2
  ADC Biosynth 2024, Redraw of Erin Gee's Biosynth circuit v3.0 2018, T1

custom parts:
  YwRobot Breadboard Power Supply: The YwRobot Breadboard Power Supply (MB-V2) has two power rails; they can be 5V or 3V3. Power to the module can be provided through the female USB socket or through the A10 (female) 2.1mm power jack.
